# Fritzing sketch flora_accelerometer_compass_sensor (saved by Fritzing 0.9.3b)

parts:
  Part1 = Adafruit Flora [part_number="Adafruit #659"]
  Part2 = Flora LSM303 Compass+Accel

nets:
  +3V3: Part1.+3V3, Part2.3.3V
  GND: Part1.GND, Part2.GND
  N1: Part1.IO2/SDA, Part2.SCL
  N2: Part1.IO3/SCL, Part2.SDA

custom parts:
  Adafruit Flora: FLORA is Adafruit's fully-featured wearable electronics platform. It's a round, sewable, Arduino-compatible microcontroller designed to empower amazing wearables projects. The FLORA is small (1.75" diameter, weighing 4.4 grams). The FLORA has built-in USB support. Built in USB means you plug it in to program it, it just shows up - all you need is a Micro-B USB cable, no additional purchases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
  Flora LSM303 Compass+Accel: Add motion and direction sensing to your wearable FLORA project with this high precision 3-axis Accelerometer+Compass sensor. Inside are two sensors, one is a classic 3-axis accelerometer, which can tell you which direction is down towards the Earth (by measuring gravity) or how fast the board is accelerating in 3D space. The other is a magnetometer that can sense where the strongest magnetic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
