# Fritzing sketch flora_color_sensor_print (saved by Fritzing 0.9.3b)

parts:
  Part2 = Adafruit Flora [part_number="Adafruit #659"]  # not connected
  Part3 = Flora TCS34725 Color Sensor  # not connected
  CLIP1 = Alligator Clip
  CLIP2 = Alligator Clip
  CLIP3 = Alligator Clip
  CLIP4 = Alligator Clip
  CLIP5 = Alligator Clip
  CLIP6 = Alligator Clip
  CLIP7 = Alligator Clip
  CLIP8 = Alligator Clip

nets:
  N1: CLIP1.wire, CLIP2.wire
  N2: CLIP3.wire, CLIP7.wire
  N3: CLIP4.wire, CLIP5.wire
  N4: CLIP6.wire, CLIP8.wire

custom parts:
  Adafruit Flora: FLORA is Adafruit's fully-featured wearable electronics platform. It's a round, sewable, Arduino-compatible microcontroller designed to empower amazing wearables projects. The FLORA is small (1.75" diameter, weighing 4.4 grams). The FLORA has built-in USB support. Built in USB means you plug it in to program it, it just shows up - all you need is a Micro-B USB cable, no additional purchases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
  Flora TCS34725 Color Sensor: Your electronics can now see in dazzling color with this lovely color light sensor. We found the best color sensor on the market, the TCS34725, which has RGB and Clear light sensing elements. An IR blocking filter, integrated on-chip and localized to the color sensing photodiodes, minimizes the IR spectral component of the incoming light and allows color measurements to be made accurately. The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
  Alligator Clip: Alligator clip
  Alligator Clip: Alligator clip
  Alligator Clip: Alligator clip
  Alligator Clip: Alligator clip
