# Fritzing sketch flora_led_blink (saved by Fritzing 0.9.3b)

parts:
  Part2 = LED Sequin - Warm White [part_number=1758]  # not connected
  CLIP2 = Alligator Clip
  CLIP3 = Alligator Clip
  CLIP4 = Alligator Clip
  CLIP5 = Alligator Clip
  Part3 = Adafruit Flora [part_number="Adafruit #659"]  # not connected

nets:
  N1: CLIP2.wire, CLIP5.wire
  N2: CLIP3.wire, CLIP4.wire

custom parts:
  LED Sequin - Warm White: Sew a little sparkle into your wearable project with an Adafruit LED Sequin. Simply connect 3 to 6VDC to the + pin and ground to the - pin, and the LED on the board will light up. You can make the LEDs fade and twinkle by using PWM.
  Alligator Clip: Alligator clip
  Alligator Clip: Alligator clip
  Adafruit Flora: FLORA is Adafruit's fully-featured wearable electronics platform. It's a round, sewable, Arduino-compatible microcontroller designed to empower amazing wearables projects. The FLORA is small (1.75" diameter, weighing 4.4 grams). The FLORA has built-in USB support. Built in USB means you plug it in to program it, it just shows up - all you need is a Micro-B USB cable, no additional purchases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
