# Fritzing sketch flora_neopixel_rainbow (saved by Fritzing 0.9.3b)

parts:
  CLIP2 = Alligator Clip
  CLIP3 = Alligator Clip
  CLIP4 = Alligator Clip
  CLIP5 = Alligator Clip
  CLIP6 = Alligator Clip
  CLIP7 = Alligator Clip
  Part2 = Adafruit Flora [part_number="Adafruit #659"]  # not connected

nets:
  N1: CLIP2.wire, CLIP5.wire
  N2: CLIP3.wire, CLIP4.wire
  N3: CLIP6.wire, CLIP7.wire

custom parts:
  Alligator Clip: Alligator clip
  Alligator Clip: Alligator clip
  Alligator Clip: Alligator clip
  Adafruit Flora: FLORA is Adafruit's fully-featured wearable electronics platform. It's a round, sewable, Arduino-compatible microcontroller designed to empower amazing wearables projects. The FLORA is small (1.75" diameter, weighing 4.4 grams). The FLORA has built-in USB support. Built in USB means you plug it in to program it, it just shows up - all you need is a Micro-B USB cable, no additional purchases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
