# Fritzing sketch flora_neopixel_strip (saved by Fritzing 0.9.3b)

parts:
  NEOPIXEL1 = Neopixel Strip -- White (60/m) [part_number=1138]
  Part4 = Adafruit Flora [part_number="Adafruit #659"]

nets:
  N1: NEOPIXEL1.+5V, Part4.VBAT
  N2: NEOPIXEL1.DI, Part4.IO9
  GND: NEOPIXEL1.GND, Part4.GND

custom parts:
  Neopixel Strip -- White (60/m): Neopixel Strip, White, 60 pixels per meter.
  Adafruit Flora: FLORA is Adafruit's fully-featured wearable electronics platform. It's a round, sewable, Arduino-compatible microcontroller designed to empower amazing wearables projects. The FLORA is small (1.75" diameter, weighing 4.4 grams). The FLORA has built-in USB support. Built in USB means you plug it in to program it, it just shows up - all you need is a Micro-B USB cable, no additional purchases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
