# Fritzing sketch gemma_conductive_fabric (saved by Fritzing 0.9.3b)

parts:
  R1 = Resistor [tolerance=±5% resistance=47k package="1206 [SMD]"]
  Part2 = GEMMA v2

nets:
  N1: R1.Pin_0, Part2.B0
  N2: R1.Pin_1, Part2.B2

notes:
  FABRIC

custom parts:
  GEMMA v2: Love FLORA but want a bite-sized version? Look no further, GEMMA is a tiny wearable platform board with a lot of might in a 1" diameter package. Powered by a Attiny85 and programmable with an Arduino IDE over USB, you'll be able to realize any wearable project! We wanted to design a microcontroller board that was small enough to fit into any project, and low cost enough to use without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
