# Fritzing sketch gemma_force_sensor (saved by Fritzing 0.9.3b)

parts:
  Part1 = GEMMA v2
  J1 = Basic Force Sensing Resistor (FSR) [package=THT]
  R1 = Resistor [tolerance=±5% resistance=10k package="1206 [SMD]"]

nets:
  N1: Part1.B2, J1.pin_1, R1.Pin_0
  N2: Part1.GND, R1.Pin_1
  N3: Part1.Vout, J1.pin_0

custom parts:
  GEMMA v2: Love FLORA but want a bite-sized version? Look no further, GEMMA is a tiny wearable platform board with a lot of might in a 1" diameter package. Powered by a Attiny85 and programmable with an Arduino IDE over USB, you'll be able to realize any wearable project! We wanted to design a microcontroller board that was small enough to fit into any project, and low cost enough to use without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
