# Fritzing sketch gemma_led_blink (saved by Fritzing 0.9.3b)

parts:
  Part1 = GEMMA v2  # not connected
  Part2 = LED Sequin - Warm White [part_number=1758]  # not connected
  CLIP2 = Alligator Clip
  CLIP3 = Alligator Clip
  CLIP4 = Alligator Clip
  CLIP5 = Alligator Clip

nets:
  N1: CLIP2.wire, CLIP5.wire
  N2: CLIP3.wire, CLIP4.wire

custom parts:
  GEMMA v2: Love FLORA but want a bite-sized version? Look no further, GEMMA is a tiny wearable platform board with a lot of might in a 1" diameter package. Powered by a Attiny85 and programmable with an Arduino IDE over USB, you'll be able to realize any wearable project! We wanted to design a microcontroller board that was small enough to fit into any project, and low cost enough to use without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
  LED Sequin - Warm White: Sew a little sparkle into your wearable project with an Adafruit LED Sequin. Simply connect 3 to 6VDC to the + pin and ground to the - pin, and the LED on the board will light up. You can make the LEDs fade and twinkle by using PWM.
  Alligator Clip: Alligator clip
  Alligator Clip: Alligator clip
