# Fritzing sketch gemma_neopixel_ring (saved by Fritzing 0.9.3b)

parts:
  Part1 = 24 NeoPixel Ring [part_number=1586]
  Part3 = GEMMA v2

nets:
  N1: Part1.IN, Part3.B1
  GND: Part1.GND, Part3.GND
  N2: Part1.VDD, Part3.Vout

custom parts:
  24 NeoPixel Ring: 24 ultra bright smart LED NeoPixels are arranged in a circle with 2.6" (66mm) outer diameter. The rings are 'chainable' - connect the output pin of one to the input pin of another. Use only one microcontroller pin to control as many as you can chain together! Each LED is addressable as the driver chip is inside the LED. Each one has ~18mA constant current drive so the color will be very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
  GEMMA v2: Love FLORA but want a bite-sized version? Look no further, GEMMA is a tiny wearable platform board with a lot of might in a 1" diameter package. Powered by a Attiny85 and programmable with an Arduino IDE over USB, you'll be able to realize any wearable project! We wanted to design a microcontroller board that was small enough to fit into any project, and low cost enough to use without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
