# Fritzing sketch gemma_neopixel_strip (saved by Fritzing 0.9.3b)

parts:
  Part3 = GEMMA v2
  NEOPIXEL1 = Neopixel Strip -- White (60/m) [part_number=1138]

nets:
  N1: Part3.B1, NEOPIXEL1.DI
  GND: Part3.GND, NEOPIXEL1.GND
  N2: Part3.Vout, NEOPIXEL1.+5V

custom parts:
  GEMMA v2: Love FLORA but want a bite-sized version? Look no further, GEMMA is a tiny wearable platform board with a lot of might in a 1" diameter package. Powered by a Attiny85 and programmable with an Arduino IDE over USB, you'll be able to realize any wearable project! We wanted to design a microcontroller board that was small enough to fit into any project, and low cost enough to use without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
  Neopixel Strip -- White (60/m): Neopixel Strip, White, 60 pixels per meter.
