# Fritzing sketch gemma_tiltswitch_debouncer (saved by Fritzing 0.9.3b)

parts:
  Part1 = GEMMA v2  # not connected
  CLIP3 = Alligator Clip
  CLIP4 = Alligator Clip
  CLIP6 = Alligator Clip
  CLIP7 = Alligator Clip
  S1 = Tilt Switch [package=THT]  # not connected

nets:
  N1: CLIP3.wire, CLIP4.wire
  N2: CLIP6.wire, CLIP7.wire

custom parts:
  GEMMA v2: Love FLORA but want a bite-sized version? Look no further, GEMMA is a tiny wearable platform board with a lot of might in a 1" diameter package. Powered by a Attiny85 and programmable with an Arduino IDE over USB, you'll be able to realize any wearable project! We wanted to design a microcontroller board that was small enough to fit into any project, and low cost enough to use without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
  Alligator Clip: Alligator clip
  Alligator Clip: Alligator clip
